// Logisim project CPU.circ as structural Verilog: 6 circuits, main circuit DMEM
module DMEM (
  input  [15:0] ADDRESS,
  input  MemWrite,
  input  clk,
  input  MemRead,
  input  Clear,
  input  [15:0] DATA_IN,
  input  WORD_EN,
  input  ENDIANNESS,
  output [15:0] DATA_OUT
);

  wire dmem_control_1_flip_signal, dmem_control_1_sel_0, dmem_control_1_sel_1;
  wire [7:0] ram_1_data, ram_2_data;
  wire [15:0] byte_mirror_1_out, byte_selector_1_word_out;

  BYTE_MIRROR byte_mirror_1 (.IN(DATA_IN), .EN(dmem_control_1_flip_signal), .OUT(byte_mirror_1_out));
  DMEM_CONTROL dmem_control_1 (
    .ENDIANNESS(ENDIANNESS), .WORD_EN(WORD_EN), .FLIP_SIGNAL(dmem_control_1_flip_signal),
    .SEL_0(dmem_control_1_sel_0), .SEL_1(dmem_control_1_sel_1), .A0(ADDRESS[0]));
  RAM #(.addrWidth(15), .bus("separate")) ram_1 (
    .addr(ADDRESS[15:1]), .din(byte_mirror_1_out[7:0]), .data(ram_1_data), .str(MemWrite),
    .sel(dmem_control_1_sel_0), .clk(clk), .ld(MemRead), .clr(Clear));
  RAM #(.addrWidth(15), .bus("separate")) ram_2 (
    .addr(ADDRESS[15:1]), .din(byte_mirror_1_out[15:8]), .data(ram_2_data), .str(MemWrite),
    .sel(dmem_control_1_sel_1), .clk(clk), .ld(MemRead), .clr(Clear));
  BYTE_SELECTOR byte_selector_1 (
    .BYTE0(ram_1_data), .EN0(dmem_control_1_sel_0), .BYTE1(ram_2_data), .EN1(dmem_control_1_sel_1),
    .WORD_OUT(byte_selector_1_word_out));
  BYTE_MIRROR byte_mirror_2 (.IN(byte_selector_1_word_out), .EN(dmem_control_1_flip_signal), .OUT(DATA_OUT));
endmodule

module BYTE_MIRROR (
  input  [15:0] IN,
  input  EN,
  output [15:0] OUT
);

  Multiplexer #(.width(8), .enable("false")) multiplexer_1 (.in0(IN[7:0]), .in1(IN[15:8]), .out(OUT[7:0]), .sel(EN));
  Multiplexer #(.width(8), .enable("false")) multiplexer_2 (.in0(IN[15:8]), .in1(IN[7:0]), .out(OUT[15:8]), .sel(EN));
endmodule

module BYTE_SELECTOR (
  input  [7:0] BYTE0,
  input  EN0,
  input  [7:0] BYTE1,
  input  EN1,
  output [15:0] WORD_OUT
);

  Multiplexer #(.width(8), .enable("false")) multiplexer_1 (
    .in0({8{1'b0}}), .in1(BYTE0), .out(WORD_OUT[7:0]), .sel(EN0));
  Multiplexer #(.width(8), .enable("false")) multiplexer_2 (
    .in0({8{1'b0}}), .in1(BYTE1), .out(WORD_OUT[15:8]), .sel(EN1));
endmodule

module DMEM_CONTROL (
  input  A0,
  input  WORD_EN,
  input  ENDIANNESS,
  output SEL_0,
  output SEL_1,
  output FLIP_SIGNAL
);

  or or_1 (SEL_0, ~A0, WORD_EN);  // OR_Gate
  or or_2 (SEL_1, A0, WORD_EN);
  Multiplexer #(.enable("false")) multiplexer_1 (.in0(A0), .in1(ENDIANNESS), .out(FLIP_SIGNAL), .sel(WORD_EN));
endmodule

module IMEM (
  input  [15:0] ADDRESS,
  input  [15:0] INSTRUCTION_IN,
  input  MemWrite,
  input  clk,
  input  MemRead,
  input  Clear,
  output [15:0] INSTRUCTION_OUT
);

  RAM #(.addrWidth(15), .dataWidth(16), .bus("separate")) ram_1 (
    .addr(ADDRESS[15:1]), .din(INSTRUCTION_IN), .data(INSTRUCTION_OUT), .str(MemWrite), .sel(1'b1),
    .clk(clk), .ld(MemRead), .clr(Clear));
endmodule

module ALU (
  input  [2:0] OPERATION,
  input  [15:0] OPERAND_1,
  input  [15:0] OPERAND_2,
  output [15:0] ALU_RES,
  output carry,
  output borrow,
  output greater,
  output zero,
  output less
);

  wire adder_1_cout, comparator_1_eq, comparator_1_gt, comparator_1_lt, decoder_1_out0, decoder_1_out1,
       decoder_1_out2, decoder_1_out3, decoder_1_out4, subtractor_1_bout;
  wire [15:0] adder_1_out, and_1_out, or_1_out, subtractor_1_out;

  assign ALU_RES = decoder_1_out0 ? and_1_out : 16'bz;  // Controlled_Buffer controlled_buffer_1
  assign and_1_out = OPERAND_1 & OPERAND_2;  // AND_Gate and_1, 16 bits wide
  assign ALU_RES = decoder_1_out1 ? or_1_out : 16'bz;  // Controlled_Buffer controlled_buffer_2
  assign or_1_out = OPERAND_1 | OPERAND_2;  // OR_Gate or_1, 16 bits wide
  Adder #(.width(16)) adder_1 (.a(OPERAND_1), .b(OPERAND_2), .out(adder_1_out), .cin(1'b0), .cout(adder_1_cout));
  assign ALU_RES = decoder_1_out2 ? adder_1_out : 16'bz;  // Controlled_Buffer controlled_buffer_3
  assign carry = decoder_1_out2 ? adder_1_cout : 1'bz;  // Controlled_Buffer controlled_buffer_4
  Subtractor #(.width(16)) subtractor_1 (
    .a(OPERAND_1), .b(OPERAND_2), .out(subtractor_1_out), .bin(1'b0), .bout(subtractor_1_bout));
  assign ALU_RES = decoder_1_out3 ? subtractor_1_out : 16'bz;  // Controlled_Buffer controlled_buffer_5
  assign borrow = decoder_1_out3 ? subtractor_1_bout : 1'bz;  // Controlled_Buffer controlled_buffer_6
  assign greater = decoder_1_out4 ? comparator_1_gt : 1'bz;  // Controlled_Buffer controlled_buffer_7
  assign zero = decoder_1_out4 ? comparator_1_eq : 1'bz;  // Controlled_Buffer controlled_buffer_8
  Comparator #(.width(16)) comparator_1 (
    .a(OPERAND_1), .b(OPERAND_2), .gt(comparator_1_gt), .eq(comparator_1_eq), .lt(comparator_1_lt));
  assign less = decoder_1_out4 ? comparator_1_lt : 1'bz;  // Controlled_Buffer controlled_buffer_9
  Decoder #(.select(3), .enable("false")) decoder_1 (
    .out0(decoder_1_out0), .out1(decoder_1_out1), .out2(decoder_1_out2), .out3(decoder_1_out3),
    .out4(decoder_1_out4), .sel(OPERATION));  // open: out5, out6, out7
endmodule
